# Fritzing sketch DiagramaSBC (saved by Fritzing 0.9.3b)
breadboards: 1

parts:
  Part1 = Soil Moisture Sensor
  Part2 = Adafruit HUZZAH32 ESP32 Feather [part_number="Adafruit #3405"]
  U1 = RELAY [package=relay-jzc]
  Part7 = Humidity Sensor - HIH-4030 Breakout
  Part8 = Humidity Sensor - HIH-4030 Breakout

nets:
  N1: Part1.SIG, Part2.A0_DAC2
  GND: Part1.GND, Part2.GND, U1.NC, Part7.GND, Part8.GND
  VCC: Part1.VCC, Part2.3.3V, U1.NO, Part7.VCC, Part8.VCC
  N2: Part2.A3_I39, Part8.OUT
  N3: Part2.A2_I34, Part7.OUT
  N4: Part2.A1_DAC1, U1.COIL2

notes:
  FC22 0.5 - 4.5 V
  0kg - 22.67kg
  Relación directamente proporcional
  Simula un sensor de presion FC22
  Simula un sensor de agua. (Se usa como sensor de fugas en nuestro proyecto).
  Leyenda:
  Rojo: VCC (3.3 V)
  Azul: GND
  Naranja: Señal humedad
  Amarillo: Señal rele
  Verde: Señal presion
  Morado: Señal fugas.
  La placa que aqui observamos no tiene el mismo encapsulado que la utilizada en el proyecto. Para mas información mirar manual.
